# Fritzing sketch FRITZING_CKT_FINAL (saved by Fritzing 0.9.3b)
circuit board: 8.46667cm x 5.64444cm
breadboards: 1

parts:
  Part1 = Arduino Uno (Rev3) - ICSP
  IC1 = ULN2003A [package="DIP16 [THT]"]
  M1 = Stepper Motor - Unipolar
  LD1 = LD
  J1 = Power Jack [package=power_jack_combo]

nets:
  N1: Part1.D8, IC1.In_1
  N2: Part1.D9_PWM, IC1.In_2
  N3: Part1.D10_PWM/SS, IC1.In_3
  N4: Part1.D11_PWM/MOSI, IC1.In_4
  N5: Part1.5V, LD1.anode
  GND: Part1.GND, IC1.0V, LD1.cathode, J1.GND
  N6: IC1.COM_-_Common, M1.COMMON_1, M1.COMMON_2, J1.PWR
  N7: IC1.Out_4, M1.D
  N8: IC1.Out_3, M1.B
  N9: IC1.Out_2, M1.C
  N10: IC1.Out_1, M1.A

custom parts:
  LD: A Generic Red Dot Laser Diode Module (~5mW)

// code stored in the sketch: FINAL.ino
#include <Stepper.h>

const int stepsPerRevolution = 48;  // according to the specification of the stepper motor used

Stepper myStepper(stepsPerRevolution, 8, 9, 10, 11);

int steps = 0;         // number of steps the motor has taken

void setup() 
{
  pinMode(8,1);
  pinMode(9,1);
  pinMode(10,1);
  pinMode(11,1);
  Serial.begin(9600);
}

void StepCount()
{
  if (steps<48)
  steps++;
  else if (steps==48)
  steps=0;
}

void StepperStep()
{
  if (Serial.available())
  {
    if (steps<48)
    {
      char data=Serial.read();
      if (data=='1') // The arduino is controlled using Pyserial Command from Python GUI Window using Keypress 1
      {
        myStepper.step(1);
        delay(50);
        Serial.print('.');
        StepCount();
      }  
    }
  }  
}


void loop() 
{
  StepperStep();
}
